# Fritzing sketch IV_Swinger (saved by Fritzing 0.9.1b)
circuit board: 8.46667cm x 5.64444cm
breadboards: 2

parts:
  ADC = ADS1115 16-bit ADC Breakout
  Op_Amp1 = TLV2462 [package=dip08]
  Rf = Resistor [tolerance=±5% resistance=82k package=THT]
  Rg = Resistor [tolerance=±5% resistance=1.5k package=THT]
  R3 = Resistor [tolerance=±5% resistance=5.6k package=THT]
  R2 = Resistor [tolerance=±5% resistance=8.2k package=THT]
  D0 = Schottky Diode [part_number=1N5819 package="Melf DO-213 AB [SMD]"]
  D1 = Schottky Diode [part_number=1N5819 package="Melf DO-213 AB [SMD]"]
  D3 = Schottky Diode [part_number=1N5819 package="Melf DO-213 AB [SMD]"]
  D2 = Schottky Diode [part_number=1N5819 package="Melf DO-213 AB [SMD]"]
  RELAY_HI_PWR = female pin header, 3 pins [form="♀ (female)"]
  RELAY_LO_PWR = female pin header, 3 pins [form="♀ (female)"]
  PV- = rounded female alternating pin header, 1 pin [form="♀ (female rounded)"]
  PV+ = rounded female alternating pin header, 1 pin [form="♀ (female rounded)"]
  LOAD_BANK_LO = rounded female pin header, 1 pin [form="♀ (female rounded)"]
  DPST_A = SWITCH-SPST-2 [package=switch-spst-vertical]
  DPST_B = SWITCH-SPST-2 [package=switch-spst-vertical]
  SHUNT = Resistor [tolerance=±0.05% resistance=75m package=THT]
  LOAD_BANK = Rotary Potentiometer (Large) [maximum_resistance=35Ω package=THT]
  LOAD_BANK_HI = female pin header, 1 pin [form="♀ (female)"]
  R1 = Resistor [tolerance=±5% resistance=180k package=THT]
  C1 = Electrolytic Capacitor [capacitance=4.7µF voltage=0.1kV package="100 mil [THT, electrolytic]"]
  R4 = Resistor [tolerance=±5% resistance=82 package=THT]
  DS1307_RTC_Module = mystery part, 5 pins [chip_label=DS1307]
  D4 = Schottky Diode [part_number=1N5819 package="300 mil [THT]"]
  Piezo_Buzzer = Piezo Speaker
  R4_2 = Resistor [tolerance=±5% resistance=1k package=THT]
  2N2222a = NPN-Transistor [package="TO92 [THT]"]
  R6 = Resistor [tolerance=±5% resistance=1k package=THT]
  R5 = Resistor [tolerance=±5% resistance=1k package=THT]
  R9 = Resistor [tolerance=±5% resistance=10k package=THT]
  R10 = Resistor [tolerance=±5% resistance=10k package=THT]
  LCD_Contrast_Pot = TRIMPOT [package=3386u]
  Shutdown_Pushbutton = Round Pushbutton
  Raspberry_Pi = Raspberry Pi B+
  SPIO_A0-A7 = female pin header, 8 pins [form="♀ (female)"]
  SPIO_B7-B0 = female pin header, 8 pins [form="♀ (female)"]
  SPIO_RPIO_EXT_1 = female pin header, 8 pins [form="♀ (female)"]
  LCD = LCD screen
  Micro_USB_Breakout_Pins = female pin header, 5 pins [form="♀ (female)"]
  SPIO_PWR = female pin header, 3 pins [form="♀ (female)"]
  SPIO_RPIO_EXT_0 = female pin header, 8 pins [form="♀ (female)"]  # not connected
  Battery_2_1A_USB = female pin header, 1 pin [form="♀ (female)"]
  Battery_1_3A_USB = female pin header, 1 pin [form="♀ (female)"]
  Battery_Charger_In = female pin header, 1 pin [form="♀ (female)"]  # not connected
  RPi_USB_PWR = female pin header, 1 pin [form="♀ (female)"]
  Micro_USB_Breakout_PWR = female pin header, 1 pin [form="♀ (female)"]
  SPIO_I2C = female pin header, 4 pins [form="♀ (female)"]
  RELAY_HI_CONTROL = female pin header, 10 pins [form="♀ (female)"]
  RELAY_LO_CONTROL = female pin header, 10 pins [form="♀ (female)"]
  SPIO_GND_1 = female pin header, 8 pins [form="♀ (female)"]
  SPIO_GND_0 = female pin header, 8 pins [form="♀ (female)"]  # not connected

nets:
  5V: ADC.VDD, Op_Amp1.A_V+, D0.cathode, D2.cathode, DS1307_RTC_Module.pin2, D4.cathode, Piezo_Buzzer.pin2, LCD_Contrast_Pot.CCW, LCD.VDD, LCD.LED+, SPIO_I2C.pin1, RELAY_HI_CONTROL.pin10, RELAY_LO_CONTROL.pin10
  GND: ADC.GND, ADC.ADDR, ADC.A3, Op_Amp1.A_V-, Rg.Pin_0, R3.Pin_0, D1.anode, D3.anode, PV-.pin1, SHUNT.Pin_0, DS1307_RTC_Module.pin1, 2N2222a.E, R9.Pin_0, R10.Pin_0, LCD_Contrast_Pot.CW, LCD.VSS, LCD.R/W, LCD.LED-, Micro_USB_Breakout_Pins.pin5, SPIO_I2C.pin2, RELAY_LO_CONTROL.pin1, SPIO_GND_1.pin8
  N1: ADC.SCL, DS1307_RTC_Module.pin4, Raspberry_Pi.GPIO3, SPIO_I2C.pin3
  N2: ADC.SDA, DS1307_RTC_Module.pin3, Raspberry_Pi.GPIO2, SPIO_I2C.pin4
  N3: ADC.A0, R2.Pin_0, D0.anode, D1.cathode
  N4: ADC.A1, R3.Pin_1, R2.Pin_1, D3.cathode, D2.anode
  N5: ADC.A2, Op_Amp1.A_OUT, Rf.Pin_1
  N6: Op_Amp1.A_-IN, Rf.Pin_0, Rg.Pin_1
  N7: Op_Amp1.A_+IN, LOAD_BANK_LO.pin1, SHUNT.Pin_1, LOAD_BANK.leg2
  N8: RELAY_HI_PWR.pin1, RELAY_LO_PWR.pin1, Micro_USB_Breakout_Pins.pin1
  N9: RELAY_LO_PWR.pin3, RELAY_HI_CONTROL.pin1
  N10: PV+.pin1, DPST_A.O, R1.Pin_1, R4.Pin_1
  N11: DPST_A.P, LOAD_BANK.wiper, LOAD_BANK_HI.pin1, C1.-
  N12: DPST_B.O, R5.Pin_1, R9.Pin_1
  3.3V: DPST_B.P, Shutdown_Pushbutton.leg1, SPIO_PWR.pin1
  N13: C1.+, R4.Pin_0
  N14: D4.anode, Piezo_Buzzer.pin1, 2N2222a.C
  N15: R4_2.Pin_0, 2N2222a.B
  N16: R4_2.Pin_1, Raspberry_Pi.GPIO18, SPIO_RPIO_EXT_1.pin7
  N17: R6.Pin_0, Raspberry_Pi.GPIO5
  N18: R6.Pin_1, R10.Pin_1, Shutdown_Pushbutton.leg0
  N19: R5.Pin_0, Raspberry_Pi.GPIO4, SPIO_RPIO_EXT_1.pin1
  N20: LCD_Contrast_Pot.WIPER, LCD.V0
  N21: Raspberry_Pi.GPIO17, SPIO_RPIO_EXT_1.pin8, LCD.DB5
  N22: Raspberry_Pi.GPIO27, SPIO_RPIO_EXT_1.pin6, LCD.DB6
  N23: Raspberry_Pi.GPIO22, SPIO_RPIO_EXT_1.pin5, LCD.DB7
  N24: Raspberry_Pi.GPIO25, SPIO_RPIO_EXT_1.pin2, LCD.RS
  N25: Raspberry_Pi.GPIO24, SPIO_RPIO_EXT_1.pin3, LCD.E
  N26: Raspberry_Pi.GPIO23, SPIO_RPIO_EXT_1.pin4, LCD.DB4
  N27: SPIO_A0-A7.pin1, RELAY_HI_CONTROL.pin9
  N28: SPIO_A0-A7.pin2, RELAY_HI_CONTROL.pin8
  N29: SPIO_A0-A7.pin3, RELAY_HI_CONTROL.pin7
  N30: SPIO_A0-A7.pin4, RELAY_HI_CONTROL.pin6
  N31: SPIO_A0-A7.pin5, RELAY_HI_CONTROL.pin5
  N32: SPIO_A0-A7.pin6, RELAY_HI_CONTROL.pin4
  N33: SPIO_A0-A7.pin7, RELAY_HI_CONTROL.pin3
  N34: SPIO_A0-A7.pin8, RELAY_HI_CONTROL.pin2
  N35: SPIO_B7-B0.pin1, RELAY_LO_CONTROL.pin9
  N36: SPIO_B7-B0.pin2, RELAY_LO_CONTROL.pin8
  N37: SPIO_B7-B0.pin3, RELAY_LO_CONTROL.pin7
  N38: SPIO_B7-B0.pin4, RELAY_LO_CONTROL.pin6
  N39: SPIO_B7-B0.pin5, RELAY_LO_CONTROL.pin5
  N40: SPIO_B7-B0.pin6, RELAY_LO_CONTROL.pin4
  N41: SPIO_B7-B0.pin7, RELAY_LO_CONTROL.pin3
  N42: SPIO_B7-B0.pin8, RELAY_LO_CONTROL.pin2
  N43: SPIO_PWR.pin2, SPIO_PWR.pin3
  N44: Battery_2_1A_USB.pin1, Micro_USB_Breakout_PWR.pin1
  N45: Battery_1_3A_USB.pin1, RPi_USB_PWR.pin1

notes:
  HALF
  OPEN
  TWO
  THREE
  FOUR
  FIVE
  SIX
  SEVEN
  EIGHT
  NINE
  TEN
  ELEVEN
  TWELVE
  THIRTEEN
  FOURTEEN
  +
  -
  Relays
  Immersion Coil Loads
  50W Resistor Loads
  Shunt Resistor
  DPST Switch
  PV Panel
  PV- cable
  PV+ cable
  (ignore the orange "wire")
  Snubber
  Piezo Buzzer (on back)
  Shutdown Pushbutton
  Raspberry Pi B+
  16x2 LCD Display
  Battery Pack
  A0  A1  A2  A3  A4  A5  A6  A7
  B7  B6  B5  B4  B3  B2  B1  B0
  GND IN1 IN2 IN3 IN4 IN5 IN6 IN7 IN8 VCC
  GND VCC JD-VCC
  GND ID D+ D- 5V
  Relay coil power (2.1A)
  5.0   3.3
  jumper
  RPi power (1.3A)
  with Slice of PI/O
  IV Swinger Schematic
  ONE
  Charger Cable
  RELAY_HI
  RELAY_LO
  IV Swinger, IV Swinger system schematic, 1.0
  The IV Swinger is an open source hardware and software project
  Permission to use the hardware design is granted under the terms of the TAPR Open Hardware License Version 1.0 (May 25, 2007) - http://www.tapr.org/OHL
  Permission to use the software is granted under the terms of the GNU GPL v3
  Current versions of the licensing files, documentation, this Fritzing file, and software can be found at:
  https://github.com/csatt/IV_Swinger
  The IV Swinger is an open source hardware and software project
  Permission to use the hardware design is granted under the terms of the TAPR Open Hardware License Version 1.0 (May 25, 2007) - http://www.tapr.org/OHL
  Permission to use the software is granted under the GNU GPL v3
  Current versions of the licensing files, documentation, this Fritzing file, and software can be found at:
  https://github.com/csatt/IV_Swinger

custom parts:
  ADS1115 16-bit ADC Breakout: ADS1015 12-bit I2C ADC+PGA Breakout
  TLV2462: Generic op-amp footprint
