# Fritzing sketch IV_Swinger2 (saved by Fritzing 0.9.3b)
breadboards: 1

parts:
  MCP3202 = IC, DIP package, 8 pins [chip_label=ADC]
  R1 = Resistor [tolerance=±5% resistance=150k package=THT]
  SHUNT = Resistor [tolerance=±0.05% resistance=5m package=THT]
  D1 = Schottky Diode [part_number=15SQ045 package="300 mil [THT]"]
  D2 = Schottky Diode [part_number=15SQ045 package="300 mil [THT]"]
  Arduino = Arduino Uno (Rev3)
  C6 = Ceramic Capacitor [capacitance=0.1µF package="100 mil [THT, multilayer]"]
  C4 = Ceramic Capacitor [capacitance=2.2nF package="100 mil [THT, multilayer]"]
  C5 = Ceramic Capacitor [capacitance=2.2nF package="100 mil [THT, multilayer]"]
  C3 = Ceramic Capacitor [capacitance=0.1µF package="100 mil [THT, multilayer]"]
  PV+ = female pin header, 1 pin [form="♀ (female)"]
  PV- = female pin header, 1 pin [form="♀ (female)"]
  TLV2462 = TLV2462 [package=dip08]
  R5 = Resistor [tolerance=±5% resistance=1k package=THT]
  Rf = Resistor [tolerance=±5% resistance=75k package=THT]
  R6 = Resistor [tolerance=±5% resistance=22k package=THT]
  C2 = Electrolytic Capacitor [capacitance=1mF package="100 mil [THT, electrolytic]"]
  R3 = Resistor [tolerance=±5% resistance=1k package=THT]
  R2 = Resistor [tolerance=±5% resistance=7.5k package=THT]
  Rg = Resistor [tolerance=±5% resistance=1k package=THT]
  R7 = Resistor [tolerance=±5% resistance=22k package=THT]
  R4 = Resistor [tolerance=±5% resistance=1k package=THT]
  C1 = Electrolytic Capacitor [capacitance=1mF package="100 mil [THT, electrolytic]"]
  Relay_Module = mystery part, 6 pins [chip_label=Relay]
  Rb = Resistor [tolerance=±5% resistance=47 package=THT]

nets:
  N1: MCP3202.pin1, Arduino.D10_PWM/SS, R6.Pin_0
  N2: MCP3202.pin2, TLV2462.B_-IN, TLV2462.B_OUT
  N3: MCP3202.pin3, TLV2462.A_OUT, Rf.Pin_0
  GND: MCP3202.pin4, SHUNT.Pin_0, D2.anode, Arduino.GND, C6.1, C4.1, C5.0, C3.1, PV-.pin1, TLV2462.A_V-, R2.Pin_1, Rg.Pin_0, Relay_Module.pin6
  N4: MCP3202.pin5, Arduino.D11_PWM/MOSI
  N5: MCP3202.pin6, Arduino.D12/MISO
  N6: MCP3202.pin7, Arduino.D13/SCK
  5V: MCP3202.pin8, Arduino.5V, C6.0, C3.0, TLV2462.A_V+, R6.Pin_1, R7.Pin_0, Relay_Module.pin5
  Vmon: R1.Pin_0, R2.Pin_0, R4.Pin_1
  N7: R1.Pin_1, D1.cathode, PV+.pin1, Relay_Module.pin1
  N8: SHUNT.Pin_1, C2.-, R3.Pin_0, C1.-, Rb.Pin_0
  N9: D1.anode, D2.cathode
  N10: Arduino.D2, R5.Pin_1, R7.Pin_1
  N11: C4.0, TLV2462.A_+IN, R3.Pin_1
  N12: C5.1, TLV2462.B_+IN, R4.Pin_0
  N13: TLV2462.A_-IN, Rf.Pin_1, Rg.Pin_1
  N14: R5.Pin_0, Relay_Module.pin4
  N15: C2.+, C1.+, Relay_Module.pin2
  N16: Relay_Module.pin3, Rb.Pin_1

custom parts:
  TLV2462: Generic op-amp footprint
