# Fritzing sketch IV_Swinger2_cell (saved by Fritzing 0.9.3b)
breadboards: 1

parts:
  MCP3202 = IC, DIP package, 8 pins [chip_label=ADC]
  SHUNT = Resistor [tolerance=±0.05% resistance=5m package=THT]
  D1 = Schottky Diode [part_number=15SQ045 package="300 mil [THT]"]
  Arduino = Arduino Uno (Rev3)
  C4 = Ceramic Capacitor [capacitance=2.2nF package="100 mil [THT, multilayer]"]
  C5 = Ceramic Capacitor [capacitance=2.2nF package="100 mil [THT, multilayer]"]
  C3 = Ceramic Capacitor [capacitance=0.1µF package="100 mil [THT, multilayer]"]
  RED1 = female pin header, 1 pin [form="♀ (female)"]
  BLK1 = female pin header, 1 pin [form="♀ (female)"]
  TLV2462 = TLV2462 [package=dip08]
  Rf = Resistor [tolerance=±5% resistance=75k package=THT]
  R5 = Resistor [tolerance=±5% resistance=22k package=THT]
  R3 = Resistor [tolerance=±5% resistance=1k package=THT]
  Rg = Resistor [tolerance=±5% resistance=1k package=THT]
  R6 = Resistor [tolerance=±5% resistance=22k package=THT]
  R4 = Resistor [tolerance=±5% resistance=1k package=THT]
  Relay_Module = mystery part, 6 pins [chip_label=Relay]
  Rb = Resistor [tolerance=±5% resistance=0 package=THT]
  C6 = Ceramic Capacitor [capacitance=0.1µF package="100 mil [THT, multilayer]"]
  Rf1_Bypass_DIP = DIP SWITCH [package=dipswitch-02]
  Rf1 = Resistor [tolerance=±5% resistance=680k package=THT]
  Second_Relay = mystery part, 6 pins [chip_label=Relay]
  R7 = Resistor [tolerance=±5% resistance=22k package=THT]
  RED2 = female pin header, 1 pin [form="♀ (female)"]
  BLK2 = female pin header, 1 pin [form="♀ (female)"]
  C2_22mF = Electrolytic Capacitor [package="200 mil [THT, electrolytic]"]
  C1_22mF = Electrolytic Capacitor [package="200 mil [THT, electrolytic]"]

nets:
  N1: MCP3202.pin1, Arduino.D10_PWM/SS, R5.Pin_0
  N2: MCP3202.pin2, TLV2462.B_-IN, TLV2462.B_OUT
  N3: MCP3202.pin3, TLV2462.A_OUT, Rf.Pin_0
  GND: MCP3202.pin4, SHUNT.Pin_0, D1.anode, Arduino.GND, C4.1, C5.0, C3.1, BLK1.pin1, TLV2462.A_V-, Rg.Pin_0, Relay_Module.pin6, C6.1
  N4: MCP3202.pin5, Arduino.D11_PWM/MOSI
  N5: MCP3202.pin6, Arduino.D12/MISO
  N6: MCP3202.pin7, Arduino.D13/SCK
  5V: MCP3202.pin8, Arduino.5V, C3.0, TLV2462.A_V+, R5.Pin_1, R6.Pin_0, Relay_Module.pin5, C6.0, R7.Pin_0
  N7: SHUNT.Pin_1, R3.Pin_0, Rb.Pin_0, C2_22mF.-, C1_22mF.-
  Vmon: D1.cathode, RED1.pin1, R4.Pin_1, Relay_Module.pin1, Second_Relay.pin3
  N8: Arduino.D2, R6.Pin_1, Relay_Module.pin4
  N9: Arduino.D4, Second_Relay.pin4, R7.Pin_1
  N10: C4.0, TLV2462.A_+IN, R3.Pin_1
  N11: C5.1, TLV2462.B_+IN, R4.Pin_0
  N12: TLV2462.A_-IN, Rg.Pin_1, Rf1_Bypass_DIP.4, Rf1.Pin_1
  N13: Rf.Pin_1, Rf1_Bypass_DIP.1, Rf1.Pin_0
  N14: Relay_Module.pin2, C2_22mF.+, C1_22mF.+
  N15: Relay_Module.pin3, Rb.Pin_1
  N16: Second_Relay.pin1, BLK2.pin1
  N17: Second_Relay.pin2, RED2.pin1

custom parts:
  TLV2462: Generic op-amp footprint
  Ceramic Capacitor: 0.1 uF multilayer Ceramic Capacitor
  Electrolytic Capacitor: electrolytic capacitor
